// Logisim project hw_vga_sim.circ as structural Verilog: 7 circuits, main circuit main
module main (
  input  nRST
);

  wire CLK, HBeginActive, HBeginPulse, HCOUNT_END, HEndActive, HEndPulse, HVisEnd, readoutctrl_1_active,
       readoutctrl_1_count0, readoutctrl_1_count1, readoutctrl_1_phase, sync_1_hsync_out, sync_1_hvis,
       sync_1_vis, sync_1_vsync_out, sync_1_vvis, VActive, VBeginActive, VBeginPulse, VCOUNT_END,
       VCOUNT_ZERO, VEndActive, VEndPulse, VVisEnd;
  wire [11:0] HCOUNT_OUT, VCOUNT_OUT;

  Clock u_CLK (.out(CLK));
  HCount hcount_1 (
    .CLK(CLK), .nRST(nRST), .HCOUNT_OUT(HCOUNT_OUT), .HCOUNT_END(HCOUNT_END), .BeginPulse(HBeginPulse),
    .EndPulse(HEndPulse), .HVisEnd(HVisEnd), .BeginActive(HBeginActive), .EndActive(HEndActive));
  VCount vcount_1 (
    .CLK(CLK), .nRST(nRST), .HCOUNT_END(HCOUNT_END), .VCOUNT_INCR(HBeginPulse), .VCOUNT_OUT(VCOUNT_OUT),
    .VCOUNT_END(VCOUNT_END), .BeginPulse(VBeginPulse), .EndPulse(VEndPulse), .VVisEnd(VVisEnd),
    .VCOUNT_ZERO(VCOUNT_ZERO), .VBeginActive(VBeginActive), .VEndActive(VEndActive));
  LED led_1 (.in(sync_1_hsync_out));
  Sync sync_1 (
    .CLK(CLK), .nRST(nRST), .HBeginPulse(HBeginPulse), .HEndPulse(HEndPulse), .VBeginPulse(VBeginPulse),
    .VEndPulse(VEndPulse), .HCOUNT_END(HCOUNT_END), .VCOUNT_ZERO(VCOUNT_ZERO), .HVisEnd(HVisEnd),
    .VVisEnd(VVisEnd), .VCOUNT_END(VCOUNT_END), .VEndActive(VEndActive), .HSYNC_OUT(sync_1_hsync_out),
    .VSYNC_OUT(sync_1_vsync_out), .HVis(sync_1_hvis), .VVis(sync_1_vvis), .Vis(sync_1_vis), .VActive(VActive));
  LED led_2 (.in(sync_1_vsync_out));
  LED led_3 (.in(sync_1_hvis));
  LED led_4 (.in(sync_1_vvis));
  LED led_5 (.in(sync_1_vis));
  Hex_Digit_Display hex_digit_display_1 (.value(HCOUNT_OUT[11:8]));  // open: dp
  Hex_Digit_Display hex_digit_display_2 (.value(HCOUNT_OUT[7:4]));  // open: dp
  Hex_Digit_Display hex_digit_display_3 (.value(VCOUNT_OUT[11:8]));  // open: dp
  Hex_Digit_Display hex_digit_display_4 (.value(VCOUNT_OUT[7:4]));  // open: dp
  Hex_Digit_Display hex_digit_display_5 (.value(HCOUNT_OUT[3:0]));  // open: dp
  Hex_Digit_Display hex_digit_display_6 (.value(VCOUNT_OUT[3:0]));  // open: dp
  ReadoutCtrl readoutctrl_1 (
    .CLK(CLK), .nRST(nRST), .VActive(VActive), .HBeginActive(HBeginActive), .HEndActive(HEndActive),
    .Active(readoutctrl_1_active), .Count0(readoutctrl_1_count0), .Count1(readoutctrl_1_count1),
    .Phase(readoutctrl_1_phase));
  LED led_6 (.in(readoutctrl_1_active));
  LED led_7 (.in(readoutctrl_1_count0));
  LED led_8 (.in(readoutctrl_1_count1));
  LED led_9 (.in(readoutctrl_1_phase));

  // Notes on the sheet:
  //   Start hsync pulse at 28F
  //   End hsync pulse at 2EF
  //   End of scanline at 31F
  //   Start vsync pulse at 1EA
  //   End vsync pulse at 1EC
  //   End of frame at 0
endmodule

module HCount (
  input  CLK,
  input  nRST,
  output [11:0] HCOUNT_OUT,
  output HCOUNT_END,
  output BeginPulse,
  output EndPulse,
  output HVisEnd,
  output BeginActive,
  output EndActive
);

  wire n74163_1_pin1, n74163_1_pin3, n74163_1_pin7, n74163_1_pin15, n74163_2_pin15;

  _74163 #(.ShowInternalStructure("true")) u_74163_1 (
    .pin1(n74163_1_pin1), .pin2(CLK), .pin3(n74163_1_pin3), .pin4(n74163_1_pin3), .pin5(n74163_1_pin3),
    .pin6(n74163_1_pin3), .pin7(n74163_1_pin7), .pin15(n74163_1_pin15), .pin14(HCOUNT_OUT[0]),
    .pin13(HCOUNT_OUT[1]), .pin12(HCOUNT_OUT[2]), .pin11(HCOUNT_OUT[3]), .pin10(n74163_1_pin7),
    .pin9(n74163_1_pin7));
  _74163 #(.ShowInternalStructure("true")) u_74163_2 (
    .pin1(n74163_1_pin1), .pin2(CLK), .pin3(n74163_1_pin3), .pin4(n74163_1_pin3), .pin5(n74163_1_pin3),
    .pin6(n74163_1_pin3), .pin7(n74163_1_pin15), .pin15(n74163_2_pin15), .pin14(HCOUNT_OUT[4]),
    .pin13(HCOUNT_OUT[5]), .pin12(HCOUNT_OUT[6]), .pin11(HCOUNT_OUT[7]), .pin10(n74163_1_pin15),
    .pin9(n74163_1_pin7));
  _74163 #(.ShowInternalStructure("true")) u_74163_3 (
    .pin1(n74163_1_pin1), .pin2(CLK), .pin3(n74163_1_pin3), .pin4(n74163_1_pin3), .pin5(n74163_1_pin3),
    .pin6(n74163_1_pin3), .pin7(n74163_2_pin15), .pin14(HCOUNT_OUT[8]), .pin13(HCOUNT_OUT[9]),
    .pin12(HCOUNT_OUT[10]), .pin11(HCOUNT_OUT[11]), .pin10(n74163_2_pin15), .pin9(n74163_1_pin7));  // open: pin15
  HCntCtrl hcntctrl_1 (
    .HCOUNT(HCOUNT_OUT), .nRST(nRST), .HCOUNT_END(HCOUNT_END), .nHCCLR(n74163_1_pin1),
    .BeginPulse(BeginPulse), .EndPulse(EndPulse), .HVisEnd(HVisEnd), .BeginActive(BeginActive),
    .EndActive(EndActive));
  // also tied to GND on the sheet: n74163_1_pin3
  // also tied to VCC on the sheet: n74163_1_pin7

  // Notes on the sheet:
  //   Counters reset when nRST or HCOUNT_END asserted
endmodule

module VCount (
  input  CLK,
  input  nRST,
  input  HCOUNT_END,
  input  VCOUNT_INCR,
  output [11:0] VCOUNT_OUT,
  output VCOUNT_END,
  output BeginPulse,
  output EndPulse,
  output VVisEnd,
  output VCOUNT_ZERO,
  output VBeginActive,
  output VEndActive
);

  wire n74163_1_pin1, n74163_1_pin7, n74163_1_pin15, n74163_2_pin15, n74163_3_pin5;
  wire [9:0] n74163_1_pin3;

  _74163 #(.ShowInternalStructure("true")) u_74163_1 (
    .pin1(n74163_1_pin1), .pin2(CLK), .pin3(n74163_1_pin3[0]), .pin4(n74163_1_pin3[1]),
    .pin5(n74163_1_pin3[2]), .pin6(n74163_1_pin3[3]), .pin7(n74163_1_pin7), .pin15(n74163_1_pin15),
    .pin14(VCOUNT_OUT[0]), .pin13(VCOUNT_OUT[1]), .pin12(VCOUNT_OUT[2]), .pin11(VCOUNT_OUT[3]),
    .pin10(VCOUNT_INCR), .pin9(nRST));
  _74163 #(.ShowInternalStructure("true")) u_74163_2 (
    .pin1(n74163_1_pin1), .pin2(CLK), .pin3(n74163_1_pin3[4]), .pin4(n74163_1_pin3[5]),
    .pin5(n74163_1_pin3[6]), .pin6(n74163_1_pin3[7]), .pin7(n74163_1_pin15), .pin15(n74163_2_pin15),
    .pin14(VCOUNT_OUT[4]), .pin13(VCOUNT_OUT[5]), .pin12(VCOUNT_OUT[6]), .pin11(VCOUNT_OUT[7]),
    .pin10(n74163_1_pin15), .pin9(nRST));
  VCntCtrl vcntctrl_1 (
    .VCOUNT(VCOUNT_OUT), .HCOUNT_END(HCOUNT_END), .VCOUNT_INCR(VCOUNT_INCR), .VCOUNT_END(VCOUNT_END),
    .nVCCLR(n74163_1_pin1), .BeginPulse(BeginPulse), .EndPulse(EndPulse), .VVisEnd(VVisEnd),
    .VCOUNT_ZERO(VCOUNT_ZERO), .VBeginActive(VBeginActive), .VEndActive(VEndActive));
  _74163 #(.ShowInternalStructure("true")) u_74163_3 (
    .pin1(n74163_1_pin1), .pin2(CLK), .pin3(n74163_1_pin3[8]), .pin4(n74163_1_pin3[9]), .pin5(n74163_3_pin5),
    .pin6(n74163_3_pin5), .pin7(n74163_2_pin15), .pin14(VCOUNT_OUT[8]), .pin13(VCOUNT_OUT[9]),
    .pin12(VCOUNT_OUT[10]), .pin11(VCOUNT_OUT[11]), .pin10(n74163_2_pin15), .pin9(nRST));  // open: pin15
  // also tied to GND on the sheet: {n74163_1_pin3[2], n74163_1_pin3[4], n74163_1_pin3[5], n74163_1_pin3[6], n74163_1_pin3[7], n74163_1_pin3[8], n74163_3_pin5}
  // also tied to VCC on the sheet: {n74163_1_pin3[0], n74163_1_pin3[1], n74163_1_pin3[3], n74163_1_pin3[9], n74163_1_pin7}

  // Notes on the sheet:
  //   Initial VCOUNT
endmodule

module HCntCtrl (
  input  [11:0] HCOUNT,
  input  nRST,
  output HCOUNT_END,
  output nHCCLR,
  output BeginPulse,
  output EndPulse,
  output HVisEnd,
  output BeginActive,
  output EndActive
);

  wire not_1_out, not_2_out, not_3_out, not_4_out, not_5_out, not_6_out, not_7_out, not_8_out, not_9_out,
       not_10_out, not_11_out, not_12_out, or_1_out;

  not not_1 (not_1_out, HCOUNT[5]);
  not not_2 (not_2_out, HCOUNT[4]);
  not not_3 (not_3_out, HCOUNT[8]);
  not not_4 (not_4_out, HCOUNT[4]);
  not not_5 (not_5_out, HCOUNT[8]);
  not not_6 (not_6_out, HCOUNT[6]);
  not not_7 (not_7_out, HCOUNT[5]);
  not not_8 (not_8_out, HCOUNT[8]);
  not not_9 (not_9_out, HCOUNT[7]);
  not not_10 (not_10_out, nRST);
  not not_11 (not_11_out, HCOUNT[6]);
  not not_12 (not_12_out, HCOUNT[7]);
  Comparator #(.mode("unsigned"), .width(12)) comparator_1 (.a(HCOUNT), .b(12'h317), .eq(BeginActive));  // open: gt, lt
  Comparator #(.mode("unsigned"), .width(12)) comparator_2 (.a(HCOUNT), .b(12'h277), .eq(EndActive));  // open: gt, lt
  and and_1 (HCOUNT_END, HCOUNT[0], HCOUNT[1], HCOUNT[2], HCOUNT[3], HCOUNT[4], not_1_out, not_6_out, not_9_out, HCOUNT[8], HCOUNT[9]);
  or or_1 (or_1_out, not_10_out, HCOUNT_END);
  and and_2 (BeginPulse, HCOUNT[0], HCOUNT[1], HCOUNT[2], HCOUNT[3], not_2_out, not_7_out, not_11_out, HCOUNT[7], not_3_out, HCOUNT[9]);
  and and_3 (EndPulse, HCOUNT[0], HCOUNT[1], HCOUNT[2], HCOUNT[3], not_4_out, HCOUNT[5], HCOUNT[6], HCOUNT[7], not_5_out, HCOUNT[9]);
  and and_4 (HVisEnd, HCOUNT[0], HCOUNT[1], HCOUNT[2], HCOUNT[3], HCOUNT[4], HCOUNT[5], HCOUNT[6], not_12_out, not_8_out, HCOUNT[9]);
  not not_13 (nHCCLR, or_1_out);

  // Notes on the sheet:
  //   This circuit is intended to be equivalent to HCntCtrl.pld
  //   Counters cleared when nRST asserted or HCOUNT_END asserted
  //   HVisEnd asserted when HCOUNT=639
  //   HCOUNT_END asserted when HCOUNT=799
  //   BeginPulse asserted when HCOUNT=655
  //   EndPulse asserted when HCOUNT=751
  //   BeginActive when HCOUNT=791
  //   EndActive when HCOUNT=631
endmodule

module VCntCtrl (
  input  [11:0] VCOUNT,
  input  HCOUNT_END,
  input  VCOUNT_INCR,
  output VCOUNT_END,
  output nVCCLR,
  output BeginPulse,
  output EndPulse,
  output VVisEnd,
  output VCOUNT_ZERO,
  output VBeginActive,
  output VEndActive
);

  wire and_1_out, not_1_out, not_2_out, not_3_out, not_4_out, not_5_out, not_6_out, not_7_out, not_8_out,
       not_9_out, not_10_out, not_11_out, not_12_out, not_13_out, not_14_out, not_15_out, not_16_out,
       not_17_out, not_18_out, not_19_out, not_20_out, not_21_out, not_22_out, not_23_out, not_24_out,
       not_25_out, not_26_out, not_27_out;

  not not_1 (not_1_out, VCOUNT[0]);
  not not_2 (not_2_out, VCOUNT[1]);
  not not_3 (not_3_out, VCOUNT[4]);
  not not_4 (not_4_out, VCOUNT[5]);
  not not_5 (not_5_out, VCOUNT[0]);
  not not_6 (not_6_out, VCOUNT[2]);
  not not_7 (not_7_out, VCOUNT[0]);
  not not_8 (not_8_out, VCOUNT[1]);
  not not_9 (not_9_out, VCOUNT[0]);
  not not_10 (not_10_out, VCOUNT[1]);
  not not_11 (not_11_out, VCOUNT[0]);
  not not_12 (not_12_out, VCOUNT[1]);
  not not_13 (not_13_out, VCOUNT[7]);
  not not_14 (not_14_out, VCOUNT[8]);
  not not_15 (not_15_out, VCOUNT[6]);
  not not_16 (not_16_out, VCOUNT[7]);
  not not_17 (not_17_out, VCOUNT[4]);
  not not_18 (not_18_out, VCOUNT[4]);
  not not_19 (not_19_out, VCOUNT[2]);
  not not_20 (not_20_out, VCOUNT[3]);
  not not_21 (not_21_out, VCOUNT[2]);
  not not_22 (not_22_out, VCOUNT[3]);
  not not_23 (not_23_out, VCOUNT[8]);
  and and_1 (and_1_out, VCOUNT_END, VCOUNT_INCR);
  not not_24 (not_24_out, VCOUNT[4]);
  not not_25 (not_25_out, VCOUNT[4]);
  not not_26 (not_26_out, VCOUNT[5]);
  not not_27 (not_27_out, VCOUNT[6]);
  and and_2 (VCOUNT_END, not_1_out, not_2_out, VCOUNT[2], VCOUNT[3], not_3_out, not_4_out, not_15_out, not_16_out, not_23_out, VCOUNT[9]);
  not not_28 (nVCCLR, and_1_out);
  and and_3 (BeginPulse, HCOUNT_END, not_5_out, VCOUNT[1], not_6_out, VCOUNT[3], not_17_out, VCOUNT[5], VCOUNT[6], VCOUNT[7], VCOUNT[8]);
  and and_4 (EndPulse, HCOUNT_END, not_7_out, not_8_out, VCOUNT[2], VCOUNT[3], not_18_out, VCOUNT[5], VCOUNT[6], VCOUNT[7], VCOUNT[8]);
  and and_5 (VVisEnd, not_9_out, not_10_out, not_19_out, not_20_out, not_24_out, VCOUNT[5], VCOUNT[6], VCOUNT[7], VCOUNT[8]);
  and and_6 (VCOUNT_ZERO, not_11_out, not_12_out, not_21_out, not_22_out, not_25_out, not_26_out, not_27_out, not_13_out, not_14_out);
  Comparator #(.mode("unsigned"), .width(12)) comparator_1 (
    .a(VCOUNT), .b(12'h20b), .eq(VBeginActive));  // open: gt, lt
  Comparator #(.mode("unsigned"), .width(12)) comparator_2 (.a(VCOUNT), .b(12'h1df), .eq(VEndActive));  // open: gt, lt

  // Notes on the sheet:
  //   This circuit is intended to be equivalent to VCntCtrl.pld
  //   Clear counters if (VCOUNT_INCR & VCOUNT_END)
  //   VVisEnd generated when VCOUNT=480 (binary 111100000)
  //   VCOUNT_ZERO generated when VCOUNT=0
  //   VBeginActive generated when VCOUNT=523
  //   VEndActive generated when VCOUNT=479
  //   BeginPulse when HCOUNT_END and VCOUNT=490 (binary 111101010)
  //   EndPulse when HCOUNT_END and VCOUNT=492 (binary 111101100)
  //   VCOUNT_END when count is 524
endmodule

module Sync (
  input  CLK,
  input  nRST,
  input  HBeginPulse,
  input  HEndPulse,
  input  VBeginPulse,
  input  VEndPulse,
  input  HCOUNT_END,
  input  VCOUNT_ZERO,
  input  HVisEnd,
  input  VVisEnd,
  input  VCOUNT_END,
  input  VEndActive,
  output HSYNC_OUT,
  output VSYNC_OUT,
  output HVis,
  output VVis,
  output Vis,
  output VActive
);

  wire and_1_out, and_2_out, and_3_out, and_4_out, and_5_out, and_6_out, and_7_out, and_8_out, and_9_out,
       not_1_out, not_2_out, not_3_out, not_4_out, not_5_out, not_6_out, not_7_out, not_8_out, not_9_out,
       not_10_out, not_11_out, not_12_out, or_1_out, or_2_out, or_3_out, or_4_out, or_5_out;

  not not_1 (not_1_out, VEndActive);
  not not_2 (not_2_out, HBeginPulse);
  not not_3 (not_3_out, HEndPulse);
  not not_4 (not_4_out, VBeginPulse);
  not not_5 (not_5_out, VEndPulse);
  not not_6 (not_6_out, nRST);
  not not_7 (not_7_out, VVisEnd);
  not not_8 (not_8_out, HCOUNT_END);
  not not_9 (not_9_out, HCOUNT_END);
  not not_10 (not_10_out, HVisEnd);
  and and_1 (and_1_out, nRST, HCOUNT_END, VCOUNT_ZERO);
  and and_2 (and_2_out, nRST, not_7_out, VVis);
  and and_3 (and_3_out, nRST, VVisEnd, not_8_out, VVis);
  and and_4 (and_4_out, nRST, HCOUNT_END, VCOUNT_END);
  and and_5 (and_5_out, nRST, not_1_out, VActive);
  and and_6 (and_6_out, nRST, VEndActive, not_9_out, VActive);
  and and_7 (and_7_out, not_2_out, not_3_out, HSYNC_OUT);
  and and_8 (and_8_out, not_4_out, not_5_out, VSYNC_OUT);
  and and_9 (and_9_out, not_10_out, HVis);
  or or_1 (or_1_out, not_11_out, HEndPulse, and_7_out);
  or or_2 (or_2_out, not_12_out, VEndPulse, and_8_out);
  D_Flip_Flop d_ff_1 (.D(or_3_out), .clk(CLK), .Q(HVis), .preset(1'b0), .reset(1'b0));  // open: Qn
  or or_3 (or_3_out, not_6_out, HCOUNT_END, and_9_out);
  D_Flip_Flop d_ff_2 (.D(or_4_out), .clk(CLK), .Q(VVis), .preset(1'b0), .reset(1'b0));  // open: Qn
  or or_4 (or_4_out, and_1_out, and_2_out, and_3_out);
  or or_5 (or_5_out, and_4_out, and_5_out, and_6_out);
  not not_11 (not_11_out, nRST);
  D_Flip_Flop d_ff_3 (.D(or_1_out), .clk(CLK), .Q(HSYNC_OUT), .preset(1'b0), .reset(1'b0));  // open: Qn
  not not_12 (not_12_out, nRST);
  D_Flip_Flop d_ff_4 (.D(or_2_out), .clk(CLK), .Q(VSYNC_OUT), .preset(1'b0), .reset(1'b0));  // open: Qn
  D_Flip_Flop d_ff_5 (.D(or_5_out), .clk(CLK), .Q(VActive), .preset(1'b0), .reset(1'b0));  // open: Qn
  and and_10 (Vis, HVis, VVis);

  // Notes on the sheet:
  //   This circuit is intended to be equivalent to Sync.pld
  //   VVis is initially false
  //    (VCOUNT starts in back porch)
endmodule

module ReadoutCtrl (
  input  CLK,
  input  nRST,
  input  VActive,
  input  HBeginActive,
  input  HEndActive,
  output Active,
  output Count0,
  output Count1,
  output Phase
);

  wire and_1_out, and_2_out, and_3_out, and_4_out, and_5_out, and_6_out, and_7_out, and_8_out, not_1_out,
       not_2_out, not_3_out, not_4_out, or_1_out, or_2_out, or_3_out;

  not not_1 (not_1_out, HEndActive);
  and and_1 (and_1_out, Active, Count0, not_4_out);
  and and_2 (and_2_out, Active, not_3_out, Count1);
  and and_3 (and_3_out, Active, Count0, Count1, not_2_out);
  and and_4 (and_4_out, Active, not_4_out, Phase);
  and and_5 (and_5_out, Active, not_3_out, Phase);
  and and_6 (and_6_out, nRST, not_1_out, Active);
  and and_7 (and_7_out, nRST, HBeginActive, VActive);
  and and_8 (and_8_out, Active, not_3_out);
  or or_1 (or_1_out, and_1_out, and_2_out);
  or or_2 (or_2_out, and_3_out, and_4_out, and_5_out);
  D_Flip_Flop d_ff_1 (.D(or_3_out), .clk(CLK), .Q(Active), .preset(1'b0), .reset(1'b0));  // open: Qn
  or or_3 (or_3_out, and_6_out, and_7_out);
  D_Flip_Flop d_ff_2 (.D(and_8_out), .clk(CLK), .Q(Count0), .preset(1'b0), .reset(1'b0));  // open: Qn
  D_Flip_Flop d_ff_3 (.D(or_1_out), .clk(CLK), .Q(Count1), .preset(1'b0), .reset(1'b0));  // open: Qn
  D_Flip_Flop d_ff_4 (.D(or_2_out), .clk(CLK), .Q(Phase), .preset(1'b0), .reset(1'b0));  // open: Qn
  not not_2 (not_2_out, Phase);
  LED led_1 (.in(Count0));
  not not_3 (not_3_out, Count0);
  LED led_2 (.in(Count1));
  not not_4 (not_4_out, Count1);
  LED led_3 (.in(Phase));
endmodule
