// Logisim project hw_vga_sim.circ as structural Verilog: 7 circuits, main circuit main
module main (
  input  nRST
);

  wire CLK_out, hcount_1_beginpulse, hcount_1_endpulse, hcount_1_hcount_end, hsync_1_hsync_out,
       vcount_1_beginpulse, vcount_1_endpulse, vcount_1_vcount_end, vsync_1_vsync_out;
  wire [11:0] HCOUNT, VCOUNT;

  Clock CLK (.out(CLK_out));
  HCount hcount_1 (
    .CLK(CLK_out), .nRST(nRST), .HCOUNT_OUT(HCOUNT), .HCOUNT_END(hcount_1_hcount_end),
    .BeginPulse(hcount_1_beginpulse), .EndPulse(hcount_1_endpulse));  // open: nHCOUNT_END
  VCount vcount_1 (
    .CLK(CLK_out), .nRST(nRST), .HCOUNT_END(hcount_1_hcount_end), .VCOUNT_OUT(VCOUNT),
    .VCOUNT_END(vcount_1_vcount_end), .BeginPulse(vcount_1_beginpulse), .EndPulse(vcount_1_endpulse));  // open: nVCOUNT_END
  HSync hsync_1 (
    .CLK(CLK_out), .nRST(nRST), .BeginPulse(hcount_1_beginpulse), .EndPulse(hcount_1_endpulse),
    .HSYNC_OUT(hsync_1_hsync_out));
  VSync vsync_1 (
    .CLK(CLK_out), .BeginPulse(vcount_1_beginpulse), .EndPulse(vcount_1_endpulse), .nRST(nRST),
    .VSYNC_OUT(vsync_1_vsync_out));
  LED led_1 (.in(vcount_1_vcount_end));
  LED led_2 (.in(hsync_1_hsync_out));
  LED led_3 (.in(vsync_1_vsync_out));
  Hex_Digit_Display hex_digit_display_1 (.value(HCOUNT[11:8]));  // open: dp
  Hex_Digit_Display hex_digit_display_2 (.value(VCOUNT[11:8]));  // open: dp
  Hex_Digit_Display hex_digit_display_3 (.value(HCOUNT[7:4]));  // open: dp
  Hex_Digit_Display hex_digit_display_4 (.value(HCOUNT[3:0]));  // open: dp
  Hex_Digit_Display hex_digit_display_5 (.value(VCOUNT[7:4]));  // open: dp
  Hex_Digit_Display hex_digit_display_6 (.value(VCOUNT[3:0]));  // open: dp
endmodule

module HCount (
  input  CLK,
  input  nRST,
  output [11:0] HCOUNT_OUT,
  output HCOUNT_END,
  output nHCOUNT_END,
  output BeginPulse,
  output EndPulse
);

  wire n74163_1_pin1, n74163_1_pin3, n74163_1_pin7, n74163_1_pin15, n74163_2_pin15;

  _74163 #(.ShowInternalStructure("true")) u_74163_1 (
    .pin1(n74163_1_pin1), .pin2(CLK), .pin3(n74163_1_pin3), .pin4(n74163_1_pin3), .pin5(n74163_1_pin3),
    .pin6(n74163_1_pin3), .pin7(n74163_1_pin7), .pin15(n74163_1_pin15), .pin14(HCOUNT_OUT[0]),
    .pin13(HCOUNT_OUT[1]), .pin12(HCOUNT_OUT[2]), .pin11(HCOUNT_OUT[3]), .pin10(n74163_1_pin7),
    .pin9(n74163_1_pin7));
  _74163 #(.ShowInternalStructure("true")) u_74163_2 (
    .pin1(n74163_1_pin1), .pin2(CLK), .pin3(n74163_1_pin3), .pin4(n74163_1_pin3), .pin5(n74163_1_pin3),
    .pin6(n74163_1_pin3), .pin7(n74163_1_pin15), .pin15(n74163_2_pin15), .pin14(HCOUNT_OUT[4]),
    .pin13(HCOUNT_OUT[5]), .pin12(HCOUNT_OUT[6]), .pin11(HCOUNT_OUT[7]), .pin10(n74163_1_pin15),
    .pin9(n74163_1_pin7));
  _74163 #(.ShowInternalStructure("true")) u_74163_3 (
    .pin1(n74163_1_pin1), .pin2(CLK), .pin3(n74163_1_pin3), .pin4(n74163_1_pin3), .pin5(n74163_1_pin3),
    .pin6(n74163_1_pin3), .pin7(n74163_2_pin15), .pin14(HCOUNT_OUT[8]), .pin13(HCOUNT_OUT[9]),
    .pin12(HCOUNT_OUT[10]), .pin11(HCOUNT_OUT[11]), .pin10(n74163_2_pin15), .pin9(n74163_1_pin7));  // open: pin15
  HCntCtrl hcntctrl_1 (
    .HCOUNT(HCOUNT_OUT), .nRST(nRST), .HCOUNT_END(HCOUNT_END), .nHCOUNT_END(nHCOUNT_END),
    .nHCCLR(n74163_1_pin1), .BeginPulse(BeginPulse), .EndPulse(EndPulse));
  // also tied to GND on the sheet: n74163_1_pin3
  // also tied to VCC on the sheet: n74163_1_pin7

  // Notes on the sheet:
  //   Counters reset when nRST or nHCOUNT_END asserted
endmodule

module VCount (
  input  CLK,
  input  nRST,
  input  HCOUNT_END,
  output [11:0] VCOUNT_OUT,
  output VCOUNT_END,
  output nVCOUNT_END,
  output BeginPulse,
  output EndPulse
);

  wire n74163_1_pin1, n74163_1_pin3, n74163_1_pin7, n74163_1_pin9, n74163_1_pin15, n74163_2_pin15;

  _74163 #(.ShowInternalStructure("true")) u_74163_1 (
    .pin1(n74163_1_pin1), .pin2(CLK), .pin3(n74163_1_pin3), .pin4(n74163_1_pin3), .pin5(n74163_1_pin3),
    .pin6(n74163_1_pin3), .pin7(n74163_1_pin7), .pin15(n74163_1_pin15), .pin14(VCOUNT_OUT[0]),
    .pin13(VCOUNT_OUT[1]), .pin12(VCOUNT_OUT[2]), .pin11(VCOUNT_OUT[3]), .pin10(HCOUNT_END),
    .pin9(n74163_1_pin9));
  _74163 #(.ShowInternalStructure("true")) u_74163_2 (
    .pin1(n74163_1_pin1), .pin2(CLK), .pin3(n74163_1_pin3), .pin4(n74163_1_pin3), .pin5(n74163_1_pin3),
    .pin6(n74163_1_pin3), .pin7(n74163_1_pin15), .pin15(n74163_2_pin15), .pin14(VCOUNT_OUT[4]),
    .pin13(VCOUNT_OUT[5]), .pin12(VCOUNT_OUT[6]), .pin11(VCOUNT_OUT[7]), .pin10(n74163_1_pin15),
    .pin9(n74163_1_pin9));
  VCntCtrl vcntctrl_1 (
    .nRST(nRST), .VCOUNT(VCOUNT_OUT), .HCOUNT_END(HCOUNT_END), .VCOUNT_END(VCOUNT_END),
    .nVCOUNT_END(nVCOUNT_END), .nVCCLR(n74163_1_pin1), .BeginPulse(BeginPulse), .EndPulse(EndPulse));
  _74163 #(.ShowInternalStructure("true")) u_74163_3 (
    .pin1(n74163_1_pin1), .pin2(CLK), .pin3(n74163_1_pin3), .pin4(n74163_1_pin3), .pin5(n74163_1_pin3),
    .pin6(n74163_1_pin3), .pin7(n74163_2_pin15), .pin14(VCOUNT_OUT[8]), .pin13(VCOUNT_OUT[9]),
    .pin12(VCOUNT_OUT[10]), .pin11(VCOUNT_OUT[11]), .pin10(n74163_2_pin15), .pin9(n74163_1_pin9));  // open: pin15
  // also tied to GND on the sheet: n74163_1_pin3
  // also tied to VCC on the sheet: {n74163_1_pin7, n74163_1_pin9}

  // Notes on the sheet:
  //   Counters reset if nRST asserted or (VCOUNT_END & HCOUNT_END)
endmodule

module HSync (
  input  CLK,
  input  nRST,
  input  BeginPulse,
  input  EndPulse,
  output HSYNC_OUT
);

  wire and_1_out, not_1_out, not_2_out, not_3_out, or_1_out;

  not not_1 (not_1_out, BeginPulse);
  not not_2 (not_2_out, EndPulse);
  and and_1 (and_1_out, not_1_out, not_2_out, HSYNC_OUT);
  or or_1 (or_1_out, not_3_out, EndPulse, and_1_out);
  not not_3 (not_3_out, nRST);
  D_Flip_Flop d_ff_1 (.D(or_1_out), .clk(CLK), .Q(HSYNC_OUT), .preset(not_3_out), .reset(1'b0));  // open: Qn

  // Notes on the sheet:
  //   This circuit is intended to replicate the logic in HSync.pld
endmodule

module VSync (
  input  CLK,
  input  BeginPulse,
  input  EndPulse,
  input  nRST,
  output VSYNC_OUT
);

  wire and_1_out, not_1_out, not_2_out, not_3_out, or_1_out;

  not not_1 (not_1_out, BeginPulse);
  not not_2 (not_2_out, EndPulse);
  or or_1 (or_1_out, not_3_out, EndPulse, and_1_out);
  and and_1 (and_1_out, not_1_out, not_2_out, VSYNC_OUT);
  D_Flip_Flop d_ff_1 (.D(or_1_out), .clk(CLK), .Q(VSYNC_OUT), .preset(not_3_out), .reset(1'b0));  // open: Qn
  not not_3 (not_3_out, nRST);

  // Notes on the sheet:
  //   This circuit is intended to replicate the logic in VSync.pld
endmodule

module HCntCtrl (
  input  [11:0] HCOUNT,
  input  nRST,
  output HCOUNT_END,
  output nHCOUNT_END,
  output nHCCLR,
  output BeginPulse,
  output EndPulse
);

  wire not_1_out, not_2_out, not_3_out, not_4_out, not_5_out, not_6_out, not_7_out, not_8_out, not_9_out,
       not_10_out, or_1_out;

  not not_1 (not_1_out, HCOUNT[5]);
  not not_2 (not_2_out, HCOUNT[4]);
  not not_3 (not_3_out, HCOUNT[8]);
  not not_4 (not_4_out, HCOUNT[4]);
  not not_5 (not_5_out, HCOUNT[8]);
  not not_6 (not_6_out, HCOUNT[6]);
  not not_7 (not_7_out, HCOUNT[5]);
  not not_8 (not_8_out, HCOUNT[7]);
  not not_9 (not_9_out, nRST);
  not not_10 (not_10_out, HCOUNT[6]);
  and and_1 (HCOUNT_END, HCOUNT[0], HCOUNT[1], HCOUNT[2], HCOUNT[3], HCOUNT[4], not_1_out, not_6_out, not_8_out, HCOUNT[8], HCOUNT[9]);
  or or_1 (or_1_out, not_9_out, HCOUNT_END);
  and and_2 (BeginPulse, HCOUNT[0], HCOUNT[1], HCOUNT[2], HCOUNT[3], not_2_out, not_7_out, not_10_out, HCOUNT[7], not_3_out, HCOUNT[9]);
  and and_3 (EndPulse, HCOUNT[0], HCOUNT[1], HCOUNT[2], HCOUNT[3], not_4_out, HCOUNT[5], HCOUNT[6], HCOUNT[7], not_5_out, HCOUNT[9]);
  not not_11 (nHCOUNT_END, HCOUNT_END);
  not not_12 (nHCCLR, or_1_out);

  // Notes on the sheet:
  //   This circuit is intended to be equivalent to HCntCtrl.pld
  //   Counters cleared when nRST asserted or HCOUNT_END asserted
  //   HCOUNT_END asserted when HCOUNT=799
  //   BeginPulse asserted when HCOUNT=655
  //   EndPulse asserted when HCOUNT=751
endmodule

module VCntCtrl (
  input  nRST,
  input  [11:0] VCOUNT,
  input  HCOUNT_END,
  output VCOUNT_END,
  output nVCOUNT_END,
  output nVCCLR,
  output BeginPulse,
  output EndPulse
);

  wire and_1_out, not_1_out, not_2_out, not_3_out, not_4_out, not_5_out, not_6_out, not_7_out, not_8_out,
       not_9_out, not_10_out, not_11_out, not_12_out, not_13_out, or_1_out;

  not not_1 (not_1_out, nRST);
  not not_2 (not_2_out, VCOUNT[0]);
  not not_3 (not_3_out, VCOUNT[1]);
  not not_4 (not_4_out, VCOUNT[4]);
  not not_5 (not_5_out, VCOUNT[5]);
  and and_1 (and_1_out, VCOUNT_END, HCOUNT_END);
  not not_6 (not_6_out, VCOUNT[1]);
  not not_7 (not_7_out, VCOUNT[2]);
  not not_8 (not_8_out, VCOUNT[2]);
  not not_9 (not_9_out, VCOUNT[6]);
  not not_10 (not_10_out, VCOUNT[7]);
  not not_11 (not_11_out, VCOUNT[4]);
  not not_12 (not_12_out, VCOUNT[4]);
  not not_13 (not_13_out, VCOUNT[8]);
  or or_1 (or_1_out, not_1_out, and_1_out);
  and and_2 (VCOUNT_END, not_2_out, not_3_out, VCOUNT[2], VCOUNT[3], not_4_out, not_5_out, not_9_out, not_10_out, not_13_out, VCOUNT[9]);
  not not_14 (nVCCLR, or_1_out);
  and and_3 (BeginPulse, HCOUNT_END, VCOUNT[0], not_6_out, not_7_out, VCOUNT[3], VCOUNT[5], VCOUNT[6], VCOUNT[7], VCOUNT[8]);
  and and_4 (EndPulse, HCOUNT_END, VCOUNT[0], VCOUNT[1], not_8_out, VCOUNT[3], VCOUNT[5], VCOUNT[6], VCOUNT[7], VCOUNT[8]);
  not not_15 (nVCOUNT_END, VCOUNT_END);

  // Notes on the sheet:
  //   This circuit is intended to be equivalent to VCntCtrl.pld
  //   Clear counters if nRST asserted or (HCOUNT_END & VCOUNT_END)
  //   BeginPulse when HCOUNT_END and VCOUNT=489
  //   EndPulse when HCOUNT_END and VCOUNT=491
  //   VCOUNT_END when count is 524
endmodule
